# Fritzing sketch 90-soft-FPGA-TD4-Sketch (saved by Fritzing 1.0.4)
breadboards: 2

parts:
  Pico2 = Raspberry Pi Pico or Pico 2
  R1 = Resistor [tolerance=±5% power=0.25W resistance=300 package=THT]
  SW1 = DIP Switch 8 Position [package=dipswitch-08]
  R2 = Resistor [tolerance=±5% power=0.25W resistance=300 package=THT]
  R3 = Resistor [tolerance=±5% power=0.25W resistance=300 package=THT]
  R4 = Resistor [tolerance=±5% power=0.25W resistance=300 package=THT]
  LED2 = LED - 3mm [color="Green (560nm)" current=12mA package="3 mm [THT]"]
  LED3 = LED - 3mm [color="Green (560nm)" current=12mA package="3 mm [THT]"]
  LED4 = LED - 3mm [color="Green (560nm)" current=12mA package="3 mm [THT]"]
  LED1 = LED - 3mm [color="Green (560nm)" current=12mA package="3 mm [THT]"]
  LED5 = LED - 3mm [color="Green (560nm)" current=12mA package="3 mm [THT]"]  # not connected
  VCC1 = 4 x AAA Battery Mount [internal_resistance=0.1Ω]

nets:
  N1: Pico2.pin_3, Pico2.pin_8, Pico2.pin_13, Pico2.pin_18, Pico2.pin_23, Pico2.pin_28, Pico2.pin_33, Pico2.pin_38, Pico2.pin_42, SW1.1, SW1.2, SW1.3, SW1.4, LED2.cathode, LED3.cathode, LED4.cathode, LED1.cathode
  N2: Pico2.pin_4, R1.Pin_1
  N3: Pico2.pin_5, R2.Pin_1
  N4: Pico2.pin_6, R3.Pin_1
  N5: Pico2.pin_7, R4.Pin_1
  N6: Pico2.pin_14, SW1.16
  N7: Pico2.pin_15, SW1.15
  N8: Pico2.pin_16, SW1.14
  N9: Pico2.pin_17, SW1.13
  N10: Pico2.pin_40, VCC1.+
  N11: R1.Pin_0, LED4.anode
  N12: R2.Pin_0, LED3.anode
  N13: R3.Pin_0, LED2.anode
  N14: R4.Pin_0, LED1.anode

notes:
  6.GP4
  5.GP3
  4.GP2
  7.GP5
  17.GP13
  GND
  14.GP10
  16.GP12
  15.GP11
  VBUS
  Anode(+)
  Cathode(-)
  Short pin 短い
  Long pin 長い
  LED
  +5V
  soft-FPGA-TD4
  Normally, pull-up is required,
  but since it's configured to pull up internally in Pico2,
  pull-up resistors are not necessary.
  通常必要なプルアップ抵抗は不要（pico2の内部プルアップを使用）
  Last updated on Oct-31-2025
  by tommie.jp (GitHub: open-tommie)
  https://github.com/open-tommie/Soft-FPGA-TD4
  OUT_PORT
  MSB ~ LSB
  IN_PORT
  MSB ~ LSB
  300Ω
  USB to PC
  Debug
  Probe
  (SWD)

custom parts:
  Raspberry Pi Pico or Pico 2: Raspberry Pi Pico and Pico 2. Based around the RP2040 and RP2350 microcontrollers respectively, Picos are low cost microcontroller device bringing Raspberry Pi quality, cost, and easy of use to the microcontroller space. Jan 2021, Split part in to two versions: tht (this one) and SMD. This one will drill holes for a .1 in header in pcb to allow plugging in the module as well as providing pads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
